# Fritzing sketch fritzing (saved by Fritzing 0.8.7b)
breadboards: 1

parts:
  Part1 = TB6612FNG Breakout v11  # not connected
  Pro_Micro1 = Pro Micro  # not connected
  NRF24L1 = NRF24L01
  Part2 = OLED 2864 display module
  BATT1 = 4xAA Switchable Battery Pack w/Bare Wire
  RGB_SMD_LED1 = SMD RGB LED (WS2812) [package=5050]
  RGB_SMD_LED2 = SMD RGB LED (WS2812) [package=5050]
  M1 = DC Motor  # not connected
  M2 = DC Motor  # not connected

nets:
  VCC: NRF24L1.VCC, Part2.VCC
  N1: NRF24L1.GND, BATT1.NEG
  VSS: Part2.GND, Part2.D/C, RGB_SMD_LED1.VSS, RGB_SMD_LED2.VSS
  VCC_2: BATT1.POS, RGB_SMD_LED1.VCC, RGB_SMD_LED2.VCC
  N2: RGB_SMD_LED1.DOut, RGB_SMD_LED2.DIn

custom parts:
  Pro Micro: The SparkFun Pro Micro is a complete USB-based microcontoller development system, in a very small footprint, capable of implementing many types of projects. All programming can be done via the USB port.
  NRF24L01: NRF24L01 module
  OLED 2864 display module: Breakout board Platform Based On Arduino by Iteadstudio Principal features : Electronic Brick Ports 3.3V or 5V power supply The official support forum: support@iteadstudio.com
  4xAA Switchable Battery Pack w/Bare Wire: 4xAA Switchable Battery Pack with Bare Wire connection
